// Logisim project Oduzimac.circ as structural Verilog: 3 circuits, main circuit Poluoduzimac
// HS
module Poluoduzimac (
  input  A,
  input  B,
  output SUM,
  output CARRY
);

  wire not_1_out;

  xor xor_1 (SUM, A, B);
  not not_1 (not_1_out, A);
  and and_1 (CARRY, not_1_out, B);
endmodule

// FS
module Oduzimac (
  input  P,
  input  A,
  input  B,
  output SUB,
  output Carry
);

  wire poluoduzimac_1_carry, poluoduzimac_1_sum, poluoduzimac_2_carry;

  Poluoduzimac poluoduzimac_1 (.A(A), .B(B), .SUM(poluoduzimac_1_sum), .CARRY(poluoduzimac_1_carry));
  Poluoduzimac poluoduzimac_2 (.A(poluoduzimac_1_sum), .B(P), .SUM(SUB), .CARRY(poluoduzimac_2_carry));
  or or_1 (Carry, poluoduzimac_2_carry, poluoduzimac_1_carry);
endmodule

// SUB
module Oduzimac8bitni (
  input  [7:0] A,
  input  [7:0] B,
  output [7:0] SUB,
  output OF
);

  wire oduzimac_1_carry, oduzimac_2_carry, oduzimac_3_carry, oduzimac_4_carry, oduzimac_5_carry,
       oduzimac_6_carry, oduzimac_7_carry;

  Oduzimac oduzimac_1 (.P(A[0]), .A(B[0]), .B(1'b0), .SUB(SUB[0]), .Carry(oduzimac_1_carry));
  Oduzimac oduzimac_2 (.P(A[1]), .A(B[1]), .B(oduzimac_1_carry), .SUB(SUB[1]), .Carry(oduzimac_2_carry));
  Oduzimac oduzimac_3 (.P(A[2]), .A(B[2]), .B(oduzimac_2_carry), .SUB(SUB[2]), .Carry(oduzimac_3_carry));
  Oduzimac oduzimac_4 (.P(A[3]), .A(B[3]), .B(oduzimac_3_carry), .SUB(SUB[3]), .Carry(oduzimac_4_carry));
  Oduzimac oduzimac_5 (.P(A[4]), .A(B[4]), .B(oduzimac_4_carry), .SUB(SUB[4]), .Carry(oduzimac_5_carry));
  Oduzimac oduzimac_6 (.P(A[5]), .A(B[5]), .B(oduzimac_5_carry), .SUB(SUB[5]), .Carry(oduzimac_6_carry));
  Oduzimac oduzimac_7 (.P(A[6]), .A(B[6]), .B(oduzimac_6_carry), .SUB(SUB[6]), .Carry(oduzimac_7_carry));
  Oduzimac oduzimac_8 (.P(A[7]), .A(B[7]), .B(oduzimac_7_carry), .SUB(SUB[7]), .Carry(OF));
endmodule
