// Logisim project Pomerac.circ as structural Verilog: 8 circuits, main circuit SHL_1
// SHL1
module SHL_1 (
  input  [7:0] IN,
  output [7:0] OUT
);


  assign OUT = {IN[6:0], 1'b0};
endmodule

// SHR1
module SHR_1 (
  input  [7:0] IN,
  output [7:0] OUT
);


  assign OUT = {1'b0, IN[7:1]};
endmodule

// ROL1
module ROL_1 (
  input  [7:0] IN,
  output [7:0] OUT
);


  assign OUT = {IN[6:0], IN[7]};
endmodule

// ROR1
module ROR_1 (
  input  [7:0] IN,
  output [7:0] OUT
);


  assign OUT = {IN[0], IN[7:1]};
endmodule

module SHL (
  input  [7:0] A,
  input  [7:0] B,
  output [7:0] OUT
);

  wire [7:0] shl_1_1_out, shl_1_2_out, shl_1_3_out, shl_1_4_out, shl_1_5_out, shl_1_6_out, shl_1_7_out;

  SHL_1 shl_1_1 (.IN(A), .OUT(shl_1_1_out));
  SHL_1 shl_1_2 (.IN(shl_1_1_out), .OUT(shl_1_2_out));
  SHL_1 shl_1_3 (.IN(shl_1_2_out), .OUT(shl_1_3_out));
  SHL_1 shl_1_4 (.IN(shl_1_3_out), .OUT(shl_1_4_out));
  SHL_1 shl_1_5 (.IN(shl_1_4_out), .OUT(shl_1_5_out));
  SHL_1 shl_1_6 (.IN(shl_1_5_out), .OUT(shl_1_6_out));
  SHL_1 shl_1_7 (.IN(shl_1_6_out), .OUT(shl_1_7_out));
  Multiplexer #(.select(3), .width(8)) multiplexer_1 (
    .in0(A), .in1(shl_1_1_out), .in2(shl_1_2_out), .in3(shl_1_3_out), .in4(shl_1_4_out), .in5(shl_1_5_out),
    .in6(shl_1_6_out), .in7(shl_1_7_out), .out(OUT), .sel(B[2:0]));  // open: en
endmodule

module SHR (
  input  [7:0] A,
  input  [7:0] B,
  output [7:0] OUT
);

  wire [7:0] shr_1_1_out, shr_1_2_out, shr_1_3_out, shr_1_4_out, shr_1_5_out, shr_1_6_out, shr_1_7_out;

  SHR_1 shr_1_1 (.IN(A), .OUT(shr_1_1_out));
  SHR_1 shr_1_2 (.IN(shr_1_1_out), .OUT(shr_1_2_out));
  SHR_1 shr_1_3 (.IN(shr_1_2_out), .OUT(shr_1_3_out));
  SHR_1 shr_1_4 (.IN(shr_1_3_out), .OUT(shr_1_4_out));
  SHR_1 shr_1_5 (.IN(shr_1_4_out), .OUT(shr_1_5_out));
  SHR_1 shr_1_6 (.IN(shr_1_5_out), .OUT(shr_1_6_out));
  SHR_1 shr_1_7 (.IN(shr_1_6_out), .OUT(shr_1_7_out));
  Multiplexer #(.select(3), .width(8)) multiplexer_1 (
    .in0(A), .in1(shr_1_1_out), .in2(shr_1_2_out), .in3(shr_1_3_out), .in4(shr_1_4_out), .in5(shr_1_5_out),
    .in6(shr_1_6_out), .in7(shr_1_7_out), .out(OUT), .sel(B[2:0]));  // open: en
endmodule

module ROL (
  input  [7:0] A,
  input  [7:0] B,
  output [7:0] OUT
);

  wire [7:0] rol_1_1_out, rol_1_2_out, rol_1_3_out, rol_1_4_out, rol_1_5_out, rol_1_6_out, rol_1_7_out;

  ROL_1 rol_1_1 (.IN(A), .OUT(rol_1_1_out));
  ROL_1 rol_1_2 (.IN(rol_1_1_out), .OUT(rol_1_2_out));
  ROL_1 rol_1_3 (.IN(rol_1_2_out), .OUT(rol_1_3_out));
  ROL_1 rol_1_4 (.IN(rol_1_3_out), .OUT(rol_1_4_out));
  ROL_1 rol_1_5 (.IN(rol_1_4_out), .OUT(rol_1_5_out));
  ROL_1 rol_1_6 (.IN(rol_1_5_out), .OUT(rol_1_6_out));
  ROL_1 rol_1_7 (.IN(rol_1_6_out), .OUT(rol_1_7_out));
  Multiplexer #(.select(3), .width(8)) multiplexer_1 (
    .in0(A), .in1(rol_1_1_out), .in2(rol_1_2_out), .in3(rol_1_3_out), .in4(rol_1_4_out), .in5(rol_1_5_out),
    .in6(rol_1_6_out), .in7(rol_1_7_out), .out(OUT), .sel(B[2:0]));  // open: en
endmodule

module ROR (
  input  [7:0] A,
  input  [7:0] B,
  output [7:0] OUT
);

  wire [7:0] ror_1_1_out, ror_1_2_out, ror_1_3_out, ror_1_4_out, ror_1_5_out, ror_1_6_out, ror_1_7_out;

  ROR_1 ror_1_1 (.IN(A), .OUT(ror_1_1_out));
  ROR_1 ror_1_2 (.IN(ror_1_1_out), .OUT(ror_1_2_out));
  ROR_1 ror_1_3 (.IN(ror_1_2_out), .OUT(ror_1_3_out));
  ROR_1 ror_1_4 (.IN(ror_1_3_out), .OUT(ror_1_4_out));
  ROR_1 ror_1_5 (.IN(ror_1_4_out), .OUT(ror_1_5_out));
  ROR_1 ror_1_6 (.IN(ror_1_5_out), .OUT(ror_1_6_out));
  ROR_1 ror_1_7 (.IN(ror_1_6_out), .OUT(ror_1_7_out));
  Multiplexer #(.select(3), .width(8)) multiplexer_1 (
    .in0(A), .in1(ror_1_1_out), .in2(ror_1_2_out), .in3(ror_1_3_out), .in4(ror_1_4_out), .in5(ror_1_5_out),
    .in6(ror_1_6_out), .in7(ror_1_7_out), .out(OUT), .sel(B[2:0]));  // open: en
endmodule
