// Logisim project Sabirac.circ as structural Verilog: 3 circuits, main circuit Polusabirac
// HA
module Polusabirac (
  input  A,
  input  B,
  output Sum,
  output Carry
);

  xor xor_1 (Sum, A, B);
  and and_1 (Carry, A, B);
endmodule

// FA
module Sabirac (
  input  Carry,
  input  A,
  input  B,
  output SUM,
  output Carry_2
);

  wire polusabirac_1_carry, polusabirac_2_carry, polusabirac_2_sum;

  Polusabirac polusabirac_1 (.A(Carry), .B(polusabirac_2_sum), .Sum(SUM), .Carry(polusabirac_1_carry));
  Polusabirac polusabirac_2 (.A(A), .B(B), .Sum(polusabirac_2_sum), .Carry(polusabirac_2_carry));
  or or_1 (Carry_2, polusabirac_1_carry, polusabirac_2_carry);
endmodule

// ADD
module Sabirac8bitni (
  input  [7:0] A,
  input  [7:0] B,
  output [7:0] X_Y,
  output OF
);

  wire sabirac_1_carry_2, sabirac_2_carry_2, sabirac_3_carry_2, sabirac_4_carry_2, sabirac_5_carry_2,
       sabirac_6_carry_2, sabirac_7_carry_2;

  Sabirac sabirac_1 (.A(A[0]), .B(B[0]), .Carry(1'b0), .SUM(X_Y[0]), .Carry_2(sabirac_1_carry_2));
  Sabirac sabirac_2 (.A(A[1]), .B(B[1]), .Carry(sabirac_1_carry_2), .SUM(X_Y[1]), .Carry_2(sabirac_2_carry_2));
  Sabirac sabirac_3 (.A(A[2]), .B(B[2]), .Carry(sabirac_2_carry_2), .SUM(X_Y[2]), .Carry_2(sabirac_3_carry_2));
  Sabirac sabirac_4 (.A(A[3]), .B(B[3]), .Carry(sabirac_3_carry_2), .SUM(X_Y[3]), .Carry_2(sabirac_4_carry_2));
  Sabirac sabirac_5 (.A(A[4]), .B(B[4]), .Carry(sabirac_4_carry_2), .SUM(X_Y[4]), .Carry_2(sabirac_5_carry_2));
  Sabirac sabirac_6 (.A(A[5]), .B(B[5]), .Carry(sabirac_5_carry_2), .SUM(X_Y[5]), .Carry_2(sabirac_6_carry_2));
  Sabirac sabirac_7 (.A(A[6]), .B(B[6]), .Carry(sabirac_6_carry_2), .SUM(X_Y[6]), .Carry_2(sabirac_7_carry_2));
  Sabirac sabirac_8 (.A(A[7]), .B(B[7]), .Carry(sabirac_7_carry_2), .SUM(X_Y[7]), .Carry_2(OF));
endmodule
