// Logisim project Shitfs.circ as structural Verilog: 8 circuits, main circuit SHL_1
// SHL1
module SHL_1 (
  input  [7:0] X,
  output [7:0] out_2
);


  assign out_2 = {X[6:0], 1'b0};
endmodule

// SHR1
module SHR_1 (
  input  [7:0] in_1,
  output [7:0] out_2
);


  assign out_2 = {1'b0, in_1[7:1]};
endmodule

// ROL1
module ROL_1 (
  input  [7:0] in_1,
  output [7:0] out_2
);


  assign out_2 = {in_1[6:0], in_1[7]};
endmodule

// ROR1
module ROR_1 (
  input  [7:0] X,
  output [7:0] out_2
);


  assign out_2 = {X[0], X[7:1]};
endmodule

module SHL (
  input  [7:0] in_1,
  input  [7:0] X,
  output [7:0] out_3
);

  wire [7:0] shl_1_1_out_2, shl_1_2_out_2, shl_1_3_out_2, shl_1_4_out_2, shl_1_5_out_2, shl_1_6_out_2,
       shl_1_7_out_2;

  SHL_1 shl_1_1 (.X(in_1), .out_2(shl_1_1_out_2));
  SHL_1 shl_1_2 (.X(shl_1_1_out_2), .out_2(shl_1_2_out_2));
  SHL_1 shl_1_3 (.X(shl_1_2_out_2), .out_2(shl_1_3_out_2));
  SHL_1 shl_1_4 (.X(shl_1_3_out_2), .out_2(shl_1_4_out_2));
  SHL_1 shl_1_5 (.X(shl_1_4_out_2), .out_2(shl_1_5_out_2));
  SHL_1 shl_1_6 (.X(shl_1_5_out_2), .out_2(shl_1_6_out_2));
  SHL_1 shl_1_7 (.X(shl_1_6_out_2), .out_2(shl_1_7_out_2));
  Multiplexer #(.select(3), .width(8)) multiplexer_1 (
    .in0(in_1), .in1(shl_1_1_out_2), .in2(shl_1_2_out_2), .in3(shl_1_3_out_2), .in4(shl_1_4_out_2),
    .in5(shl_1_5_out_2), .in6(shl_1_6_out_2), .in7(shl_1_7_out_2), .out(out_3), .sel(X[2:0]));  // open: en
endmodule

module SHR (
  input  [7:0] in_1,
  input  [7:0] X,
  output [7:0] out_3
);

  wire [7:0] shr_1_1_out_2, shr_1_2_out_2, shr_1_3_out_2, shr_1_4_out_2, shr_1_5_out_2, shr_1_6_out_2,
       shr_1_7_out_2;

  SHR_1 shr_1_1 (.in_1(in_1), .out_2(shr_1_1_out_2));
  SHR_1 shr_1_2 (.in_1(shr_1_1_out_2), .out_2(shr_1_2_out_2));
  SHR_1 shr_1_3 (.in_1(shr_1_2_out_2), .out_2(shr_1_3_out_2));
  SHR_1 shr_1_4 (.in_1(shr_1_3_out_2), .out_2(shr_1_4_out_2));
  SHR_1 shr_1_5 (.in_1(shr_1_4_out_2), .out_2(shr_1_5_out_2));
  SHR_1 shr_1_6 (.in_1(shr_1_5_out_2), .out_2(shr_1_6_out_2));
  SHR_1 shr_1_7 (.in_1(shr_1_6_out_2), .out_2(shr_1_7_out_2));
  Multiplexer #(.select(3), .width(8)) multiplexer_1 (
    .in0(in_1), .in1(shr_1_1_out_2), .in2(shr_1_2_out_2), .in3(shr_1_3_out_2), .in4(shr_1_4_out_2),
    .in5(shr_1_5_out_2), .in6(shr_1_6_out_2), .in7(shr_1_7_out_2), .out(out_3), .sel(X[2:0]));  // open: en
endmodule

module ROL (
  input  [7:0] in_1,
  input  [7:0] X,
  output [7:0] out_3
);

  wire [7:0] rol_1_1_out_2, rol_1_2_out_2, rol_1_3_out_2, rol_1_4_out_2, rol_1_5_out_2, rol_1_6_out_2,
       rol_1_7_out_2;

  ROL_1 rol_1_1 (.in_1(in_1), .out_2(rol_1_1_out_2));
  ROL_1 rol_1_2 (.in_1(rol_1_1_out_2), .out_2(rol_1_2_out_2));
  ROL_1 rol_1_3 (.in_1(rol_1_2_out_2), .out_2(rol_1_3_out_2));
  ROL_1 rol_1_4 (.in_1(rol_1_3_out_2), .out_2(rol_1_4_out_2));
  ROL_1 rol_1_5 (.in_1(rol_1_4_out_2), .out_2(rol_1_5_out_2));
  ROL_1 rol_1_6 (.in_1(rol_1_5_out_2), .out_2(rol_1_6_out_2));
  ROL_1 rol_1_7 (.in_1(rol_1_6_out_2), .out_2(rol_1_7_out_2));
  Multiplexer #(.select(3), .width(8)) multiplexer_1 (
    .in0(in_1), .in1(rol_1_1_out_2), .in2(rol_1_2_out_2), .in3(rol_1_3_out_2), .in4(rol_1_4_out_2),
    .in5(rol_1_5_out_2), .in6(rol_1_6_out_2), .in7(rol_1_7_out_2), .out(out_3), .sel(X[2:0]));  // open: en
endmodule

module ROR (
  input  [7:0] in_1,
  input  [7:0] X,
  output [7:0] out_3
);

  wire [7:0] ror_1_1_out_2, ror_1_2_out_2, ror_1_3_out_2, ror_1_4_out_2, ror_1_5_out_2, ror_1_6_out_2,
       ror_1_7_out_2;

  ROR_1 ror_1_1 (.X(in_1), .out_2(ror_1_1_out_2));
  ROR_1 ror_1_2 (.X(ror_1_1_out_2), .out_2(ror_1_2_out_2));
  ROR_1 ror_1_3 (.X(ror_1_2_out_2), .out_2(ror_1_3_out_2));
  ROR_1 ror_1_4 (.X(ror_1_3_out_2), .out_2(ror_1_4_out_2));
  ROR_1 ror_1_5 (.X(ror_1_4_out_2), .out_2(ror_1_5_out_2));
  ROR_1 ror_1_6 (.X(ror_1_5_out_2), .out_2(ror_1_6_out_2));
  ROR_1 ror_1_7 (.X(ror_1_6_out_2), .out_2(ror_1_7_out_2));
  Multiplexer #(.select(3), .width(8)) multiplexer_1 (
    .in0(in_1), .in1(ror_1_1_out_2), .in2(ror_1_2_out_2), .in3(ror_1_3_out_2), .in4(ror_1_4_out_2),
    .in5(ror_1_5_out_2), .in6(ror_1_6_out_2), .in7(ror_1_7_out_2), .out(out_3), .sel(X[2:0]));  // open: en
endmodule
