// Logisim project adder.circ as structural Verilog: 4 circuits, main circuit main
module main (
  input  in_1,
  input  in_2,
  output out_3,
  output out_4
);

  xor xor_1 (out_3, in_1, in_2);
  and and_1 (out_4, in_1, in_2);
endmodule

// HA
module Half_adder (
  input  A,
  input  B,
  output Sum,
  output Carry
);

  xor xor_1 (Sum, A, B);
  and and_1 (Carry, A, B);
endmodule

// FA
module Adder (
  input  A,
  input  B,
  input  Carry,
  output Carry_2,
  output Sum
);

  wire half_adder_1_carry, half_adder_1_sum, half_adder_2_carry;

  Half_adder half_adder_1 (.A(A), .B(B), .Sum(half_adder_1_sum), .Carry(half_adder_1_carry));
  Half_adder half_adder_2 (.A(half_adder_1_sum), .B(Carry), .Sum(Carry_2), .Carry(half_adder_2_carry));
  or or_1 (Sum, half_adder_1_carry, half_adder_2_carry);
endmodule

// ADD
module Sabirac (
  input  [7:0] X,
  input  [7:0] Y,
  output [7:0] Rezultat,
  output OF
);

  wire adder_1_sum, adder_2_sum, adder_3_sum, adder_4_sum, adder_5_sum, adder_6_sum, adder_7_sum;

  Adder adder_1 (.A(X[0]), .B(Y[0]), .Carry(1'b0), .Carry_2(Rezultat[0]), .Sum(adder_1_sum));
  Adder adder_2 (.A(X[1]), .B(Y[1]), .Carry(adder_1_sum), .Carry_2(Rezultat[1]), .Sum(adder_2_sum));
  Adder adder_3 (.A(X[2]), .B(Y[2]), .Carry(adder_2_sum), .Carry_2(Rezultat[2]), .Sum(adder_3_sum));
  Adder adder_4 (.A(X[3]), .B(Y[3]), .Carry(adder_3_sum), .Carry_2(Rezultat[3]), .Sum(adder_4_sum));
  Adder adder_5 (.A(X[4]), .B(Y[4]), .Carry(adder_4_sum), .Carry_2(Rezultat[4]), .Sum(adder_5_sum));
  Adder adder_6 (.A(X[5]), .B(Y[5]), .Carry(adder_5_sum), .Carry_2(Rezultat[5]), .Sum(adder_6_sum));
  Adder adder_7 (.A(X[6]), .B(Y[6]), .Carry(adder_6_sum), .Carry_2(Rezultat[6]), .Sum(adder_7_sum));
  Adder adder_8 (.A(X[7]), .B(Y[7]), .Carry(adder_7_sum), .Carry_2(Rezultat[7]), .Sum(OF));
endmodule
