// Logisim project mov.circ as structural Verilog: 1 circuit, main circuit MOV
module MOV (
  input  [2:0] AdresaDest,
  input  [2:0] AdresaSrc
);

  wire clock_1_out;
  wire [7:0] registers_1_out_5;

  Clock clock_1 (.out(clock_1_out));
  Registers registers_1 (
    .SET({8{1'b0}}), .ADRESS(AdresaSrc), .CLK(clock_1_out), .Control(1'b1), .out_5(registers_1_out_5));
  Registers registers_2 (
    .SET(registers_1_out_5), .ADRESS(AdresaDest), .CLK(clock_1_out), .Control(1'b0));  // open: out_5
endmodule
