// Logisim project subtractor.circ as structural Verilog
// HS
module Half_Subtractor (
  input  X,
  input  Y,
  output S,
  output P
);

  wire not_1_out;

  xor xor_1 (S, X, Y);
  not not_1 (not_1_out, X);
  and and_1 (P, not_1_out, Y);
endmodule

// FS
module Full_Subtractor (
  input  X,
  input  Y,
  input  P,
  output S,
  output PP
);

  wire half_subtractor_1_p, half_subtractor_1_s, half_subtractor_2_p;

  Half_Subtractor half_subtractor_1 (.X(X), .Y(Y), .S(half_subtractor_1_s), .P(half_subtractor_1_p));
  Half_Subtractor half_subtractor_2 (.X(half_subtractor_1_s), .Y(P), .S(S), .P(half_subtractor_2_p));
  or or_1 (PP, half_subtractor_2_p, half_subtractor_1_p);
endmodule

// SUB
module Subtractor (
  input  [7:0] X,
  input  [7:0] Y,
  output [7:0] Z,
  output OF
);

  wire full_subtractor_1_pp, full_subtractor_2_pp, full_subtractor_3_pp, full_subtractor_4_pp,
       full_subtractor_5_pp, full_subtractor_6_pp, full_subtractor_7_pp;

  Full_Subtractor full_subtractor_1 (.X(X[0]), .Y(Y[0]), .P(1'b0), .S(Z[0]), .PP(full_subtractor_1_pp));
  Full_Subtractor full_subtractor_2 (.X(X[1]), .Y(Y[1]), .P(full_subtractor_1_pp), .S(Z[1]), .PP(full_subtractor_2_pp));
  Full_Subtractor full_subtractor_3 (.X(X[2]), .Y(Y[2]), .P(full_subtractor_2_pp), .S(Z[2]), .PP(full_subtractor_3_pp));
  Full_Subtractor full_subtractor_4 (.X(X[3]), .Y(Y[3]), .P(full_subtractor_3_pp), .S(Z[3]), .PP(full_subtractor_4_pp));
  Full_Subtractor full_subtractor_5 (.X(X[4]), .Y(Y[4]), .P(full_subtractor_4_pp), .S(Z[4]), .PP(full_subtractor_5_pp));
  Full_Subtractor full_subtractor_6 (.X(X[5]), .Y(Y[5]), .P(full_subtractor_5_pp), .S(Z[5]), .PP(full_subtractor_6_pp));
  Full_Subtractor full_subtractor_7 (.X(X[6]), .Y(Y[6]), .P(full_subtractor_6_pp), .S(Z[6]), .PP(full_subtractor_7_pp));
  Full_Subtractor full_subtractor_8 (.X(X[7]), .Y(Y[7]), .P(full_subtractor_7_pp), .S(Z[7]), .PP(OF));
endmodule
