// Logisim project ALU.circ as structural Verilog: 2 circuits, main circuit ALU
module ALU (
  input  [7:0] R1__Value_of_first_register,
  input  [7:0] R2__Value_of_second_register,
  input  [3:0] COM__Value_of_command__0000_to_1111,
  output [7:0] OUT__ALU_output,
  output [3:0] FLAGS_ZCOP
);

  wire oduzimac8bitni_1_of, sabirac8bitni_1_of;
  wire [7:0] and_1_out, not_1_out, oduzimac8bitni_1_sub, oduzimac8bitni_2_sub, or_1_out, rol_1_out,
       ror_1_out, sabirac8bitni_1_x_y, shl_1_out, shr_1_out;

  Sabirac8bitni sabirac8bitni_1 (
    .A(R1__Value_of_first_register), .B(R2__Value_of_second_register), .X_Y(sabirac8bitni_1_x_y),
    .OF(sabirac8bitni_1_of));
  Oduzimac8bitni oduzimac8bitni_1 (
    .A(R1__Value_of_first_register), .B(R2__Value_of_second_register), .SUB(oduzimac8bitni_1_sub),
    .OF(oduzimac8bitni_1_of));
  SHL shl_1 (.A(R1__Value_of_first_register), .B(R2__Value_of_second_register), .OUT(shl_1_out));
  SHR shr_1 (.A(R1__Value_of_first_register), .B(R2__Value_of_second_register), .OUT(shr_1_out));
  ROL rol_1 (.A(R1__Value_of_first_register), .B(R2__Value_of_second_register), .OUT(rol_1_out));
  ROR ror_1 (.A(R1__Value_of_first_register), .B(R2__Value_of_second_register), .OUT(ror_1_out));
  assign not_1_out = ~R1__Value_of_first_register;  // NOT_Gate not_1, 8 bits wide
  assign and_1_out = R2__Value_of_second_register & R1__Value_of_first_register;  // AND_Gate and_1, 8 bits wide
  assign or_1_out = R2__Value_of_second_register | R1__Value_of_first_register;  // OR_Gate or_1, 8 bits wide
  Oduzimac8bitni oduzimac8bitni_2 (
    .A(R1__Value_of_first_register), .B(R2__Value_of_second_register), .SUB(oduzimac8bitni_2_sub));  // open: OF
  Multiplexer #(.select(4), .width(8)) multiplexer_1 (
    .in0(R1__Value_of_first_register), .in1(R1__Value_of_first_register), .in2(R1__Value_of_first_register),
    .in3(sabirac8bitni_1_x_y), .in4(oduzimac8bitni_1_sub), .in5({8{1'b0}}),
    .in6(R1__Value_of_first_register), .in7(shl_1_out), .in8(shr_1_out), .in9(rol_1_out), .in10(ror_1_out),
    .in11(not_1_out), .in12(and_1_out), .in13(or_1_out), .in14(oduzimac8bitni_2_sub),
    .in15(oduzimac8bitni_2_sub), .out(OUT__ALU_output), .sel(COM__Value_of_command__0000_to_1111));  // open: en
  flag_filters flag_filters_1 (
    .IN__OF_plus(sabirac8bitni_1_of), .IN__ALU_output(OUT__ALU_output), .OUT_ZCOP(FLAGS_ZCOP),
    .IN_COM(COM__Value_of_command__0000_to_1111), .IN__OF_minus(oduzimac8bitni_1_of));
endmodule

// Flags init
module flag_filters (
  input  [7:0] IN__ALU_output,
  input  IN__OF_plus,
  input  IN__OF_minus,
  input  [3:0] IN_COM,
  output [3:0] OUT_ZCOP
);

  wire [3:0] multiplexer_1_out;
  wire [7:1] Negate_output_to_check_if_it_s_zero_out;

  Multiplexer #(.select(4)) multiplexer_1 (
    .in0(1'b0), .in1(1'b0), .in2(IN__OF_plus), .in3(IN__OF_minus), .in4(1'b0), .in5(1'b0), .in6(1'b0),
    .in7(1'b0), .in8(1'b0), .in9(1'b0), .in10(1'b0), .in11(1'b0), .in12(1'b0), .in13(1'b0), .in14(1'b0),
    .in15(1'b0), .out(multiplexer_1_out[2]), .sel(IN_COM));  // open: en
  Multiplexer #(.select(4), .width(4)) multiplexer_2 (
    .in0(4'b0000), .in1(4'b0000), .in2(4'b0000),
    .in3({multiplexer_1_out[3:2], multiplexer_1_out[2], multiplexer_1_out[0]}),
    .in4({multiplexer_1_out[3:2], multiplexer_1_out[2], multiplexer_1_out[0]}), .in5(4'b0000), .in6(4'b0000),
    .in7({multiplexer_1_out[3:2], multiplexer_1_out[2], multiplexer_1_out[0]}),
    .in8({multiplexer_1_out[3:2], multiplexer_1_out[2], multiplexer_1_out[0]}),
    .in9({multiplexer_1_out[3:2], multiplexer_1_out[2], multiplexer_1_out[0]}),
    .in10({multiplexer_1_out[3:2], multiplexer_1_out[2], multiplexer_1_out[0]}),
    .in11({multiplexer_1_out[3:2], multiplexer_1_out[2], multiplexer_1_out[0]}),
    .in12({multiplexer_1_out[3:2], multiplexer_1_out[2], multiplexer_1_out[0]}),
    .in13({multiplexer_1_out[3:2], multiplexer_1_out[2], multiplexer_1_out[0]}),
    .in14({multiplexer_1_out[3:2], multiplexer_1_out[2], multiplexer_1_out[0]}), .in15(4'b0000),
    .out(OUT_ZCOP), .sel(IN_COM));  // open: en
  assign {Negate_output_to_check_if_it_s_zero_out, multiplexer_1_out[0]} = ~IN__ALU_output;  // NOT_Gate Negate_output_to_check_if_it_s_zero, 8 bits wide
  and and_1 (multiplexer_1_out[3], Negate_output_to_check_if_it_s_zero_out[7], Negate_output_to_check_if_it_s_zero_out[6], Negate_output_to_check_if_it_s_zero_out[5], Negate_output_to_check_if_it_s_zero_out[4], Negate_output_to_check_if_it_s_zero_out[3], Negate_output_to_check_if_it_s_zero_out[2], Negate_output_to_check_if_it_s_zero_out[1], multiplexer_1_out[0]);

  // Notes on the sheet:
  //   Only gives OF if the command is ADD or SUB, else  gives 0
  //   If command is 0, 1, 2, 5, 6, 14, 15 writes zeroes in flags, else raise flags normally
endmodule
