// Logisim project BOB-CPU.circ as structural Verilog: 1 circuit, main circuit BOB
module BOB (
  output [3:0] ZCOP,
  output [7:0] ALU_OUTPUT
);

  wire CLK_out, cu_1_p4, cu_1_p5, cu_1_p7, cu_1_p8, cu_1_p9, not_1_out, not_2_out, not_3_out;
  wire [2:0] cu_1_p10, cu_1_p11, cu_1_p12;
  wire [3:0] alu_1_flags_zcop, cu_1_p13;
  wire [7:0] cu_1_p3, cu_1_p6, pc_1_cl__current_line, ram_2_data, registers_1_ax,
       registers_1_r1__value_of_first_register, registers_1_r2__value_of_second_register;
  wire [15:0] cu_1_p1;

  Clock CLK (.out(CLK_out));
  PC pc_1 (
    .CLK(CLK_out), .CL__current_line(pc_1_cl__current_line), .JMP__Input_for_JMP_command(cu_1_p3),
    .CJ__if_1__JMP_is_allowed(ZCOP[3]), .J__if_1__JMP_is_allowed(cu_1_p4));
  not not_1 (not_1_out, 1'b1);
  // CU cu_1: pin names not known; wires that end beside it: cu_1_p1, CLK_out, cu_1_p3, cu_1_p4, cu_1_p5, cu_1_p6, cu_1_p7, cu_1_p8, cu_1_p9, cu_1_p10, cu_1_p11, cu_1_p12, cu_1_p13
  RAM #(.dataWidth(16), .bus("separate")) ram_1 (
    .addr(pc_1_cl__current_line), .data(cu_1_p1), .str(not_1_out), .clk(CLK_out), .ld(1'b1));  // open: din, sel, clr
  not not_2 (not_2_out, cu_1_p8);
  RAM #(.bus("separate")) ram_2 (
    .addr(cu_1_p6), .din(registers_1_ax), .data(ram_2_data), .str(cu_1_p8), .clk(CLK_out), .ld(not_2_out));  // open: sel, clr
  not not_3 (not_3_out, cu_1_p8);
  Registers registers_1 (
    .DEST__Adress_if_register_that_loads_data(cu_1_p12),
    .R1__Value_of_first_register(registers_1_r1__value_of_first_register), .CLK(CLK_out),
    .A1__Adress_of_first_register(cu_1_p10), .S__if_1__Input_from_REG_to_DATA_is_allowed(not_3_out),
    .R2__Value_of_second_register(registers_1_r2__value_of_second_register),
    .A2__Adress_of_second_register(cu_1_p11), .MV__if_1__transfer_data_within_REG_is_allowed(cu_1_p7),
    .ALU(ALU_OUTPUT), .DATA(ram_2_data), .L__if_1__input_from_DATA_to_REG_is_allowed(cu_1_p9),
    .IF__if_1__input_into_REG_is_forbidden(cu_1_p5), .AX(registers_1_ax));
  Flags flags_1 (
    .ZCOP(alu_1_flags_zcop), .CLK(CLK_out), .PF__Parity_Flag(ZCOP[0]), .OF__Overflow_Flag(ZCOP[1]),
    .CF__Carry_Flag(ZCOP[2]), .ZF__Zero_Flag(ZCOP[3]));
  ALU alu_1 (
    .R1__Value_of_first_register(registers_1_r1__value_of_first_register),
    .R2__Value_of_second_register(registers_1_r2__value_of_second_register), .OUT__ALU_output(ALU_OUTPUT),
    .COM__Value_of_command__0000_to_1111(cu_1_p13), .FLAGS_ZCOP(alu_1_flags_zcop));

  // Notes on the sheet:
  //   INSTRUCTIONS
  //   DATA
endmodule
