// Logisim project CU.circ as structural Verilog: 3 circuits, main circuit PARSER
module CU (
  input  [15:0] INS__Instruction_value,
  input  CLK,
  output [3:0] COM__Value_of_command__0000_to_1111,
  output [2:0] A1__Adress_of_first_register,
  output [2:0] A2__Adress_of_second_register,
  output [7:0] MA__Adress_in_DATA_for_LOAD,
  output [7:0] JMP__Input_for_JMP_command,
  output [2:0] DEST__Adress_of_register_that_loads_data,
  output L__if_1__input_from_DATA_to_REG_is_allowed,
  output S__if_1__input_from_REG_to_DATA_is_allowed,
  output MV__if_1__transfer_data_within_REG_is_allowed,
  output J__if_1__JMP_is_allowed,
  output IF__if_1__input_in_REG_is_forbidden
);

  wire not_1_out;

  PARSER parser_1 (
    .Instruction(INS__Instruction_value), .COM(COM__Value_of_command__0000_to_1111),
    .A1(A1__Adress_of_first_register), .A2(A2__Adress_of_second_register), .MA(MA__Adress_in_DATA_for_LOAD));
  Control_Bits control_bits_1 (
    .in_1(COM__Value_of_command__0000_to_1111),
    .L__if_1__input_from_DATA_to_REG_is_allowed(L__if_1__input_from_DATA_to_REG_is_allowed),
    .S__if_1__input_from_REG_to_DATA_is_allowed(S__if_1__input_from_REG_to_DATA_is_allowed),
    .MV__if_1__transfer_data_within_REG_is_allowed(MV__if_1__transfer_data_within_REG_is_allowed),
    .IF__if_1__input_in_REG_is_forbidden(IF__if_1__input_in_REG_is_forbidden),
    .J__if_1__JMP_is_allowed(J__if_1__JMP_is_allowed));
  Multiplexer #(.width(3)) multiplexer_1 (
    .in0(A2__Adress_of_second_register), .in1(3'b000), .out(DEST__Adress_of_register_that_loads_data),
    .sel(L__if_1__input_from_DATA_to_REG_is_allowed));  // open: en
  Register JMP_REG (.D(MA__Adress_in_DATA_for_LOAD), .Q(JMP__Input_for_JMP_command), .clk(not_1_out));  // open: en, clr
  not not_1 (not_1_out, CLK);
endmodule

// PAR
module PARSER (
  input  [15:0] Instruction,
  output [3:0] COM,
  output [2:0] A1,
  output [2:0] A2,
  output [7:0] MA
);


  assign A1 = Instruction[6:4];
  assign A2 = Instruction[9:7];
  assign COM = Instruction[3:0];
  assign MA = Instruction[11:4];
endmodule

// CB
module Control_Bits (
  input  [3:0] in_1,
  output IF__if_1__input_in_REG_is_forbidden,
  output J__if_1__JMP_is_allowed,
  output MV__if_1__transfer_data_within_REG_is_allowed,
  output S__if_1__input_from_REG_to_DATA_is_allowed,
  output L__if_1__input_from_DATA_to_REG_is_allowed
);

  wire and_1_out, and_5_out;

  and and_1 (and_1_out, in_1[0], ~in_1[1], ~in_1[2], ~in_1[3]);  // AND_Gate
  and and_2 (S__if_1__input_from_REG_to_DATA_is_allowed, ~in_1[0], in_1[1], ~in_1[2], ~in_1[3]);  // AND_Gate
  or or_1 (L__if_1__input_from_DATA_to_REG_is_allowed, and_1_out, S__if_1__input_from_REG_to_DATA_is_allowed);
  and and_3 (MV__if_1__transfer_data_within_REG_is_allowed, ~in_1[0], ~in_1[1], ~in_1[2], ~in_1[3]);  // AND_Gate
  and and_4 (J__if_1__JMP_is_allowed, ~in_1[0], in_1[1], in_1[2], ~in_1[3]);  // AND_Gate
  or or_2 (IF__if_1__input_in_REG_is_forbidden, J__if_1__JMP_is_allowed, and_5_out);
  and and_5 (and_5_out, ~in_1[0], in_1[1], in_1[2], in_1[3]);  // AND_Gate
endmodule
