// Logisim project Flags.circ as structural Verilog: 1 circuit, main circuit Flags
// FLAGS
module Flags (
  input  CLK,
  input  [3:0] ZCOP,
  output [3:0] ZCOP_out
);

  D_Flip_Flop ZF (.clk(CLK), .D(ZCOP[3]), .Q(ZCOP_out[3]));  // open: Qn, preset, en, reset
  D_Flip_Flop CF (.clk(CLK), .D(ZCOP[2]), .Q(ZCOP_out[2]));  // open: Qn, preset, en, reset
  D_Flip_Flop OF (.clk(CLK), .D(ZCOP[1]), .Q(ZCOP_out[1]));  // open: Qn, preset, en, reset
  D_Flip_Flop PF (.clk(CLK), .D(ZCOP[0]), .Q(ZCOP_out[0]));  // open: Qn, preset, en, reset
endmodule
