// Logisim project Registers.circ as structural Verilog: 1 circuit, main circuit Registers
// REG
module Registers (
  input  CLK,
  input  in_2,
  input  [7:0] MEM,
  input  [2:0] SOURCE1,
  input  [2:0] SOURCE2,
  input  [2:0] DESTINATION,
  input  in_7,
  output [7:0] AX,
  output [7:0] VALUE1,
  output [7:0] VALUE2
);

  wire and_1_out, decoder_1_out0, decoder_1_out1, decoder_1_out2, decoder_1_out3, decoder_1_out4,
       decoder_1_out5, decoder_1_out6, decoder_1_out7, not_1_out;
  wire [7:0] BX_q, controlled_buffer_1_out, CX_q, DX_q, multiplexer_1_out, P1_q, P2_q, P3_q, PC_q;

  assign controlled_buffer_1_out = in_2 ? VALUE1 : 8'bz;  // Controlled_Buffer controlled_buffer_1
  not not_1 (not_1_out, in_2);
  Multiplexer #(.width(8)) multiplexer_1 (
    .in0(controlled_buffer_1_out), .in1(MEM), .out(multiplexer_1_out), .sel(and_1_out));  // open: en
  and and_1 (and_1_out, not_1_out, in_7);
  Decoder #(.select(3)) decoder_1 (
    .out0(decoder_1_out0), .out1(decoder_1_out1), .out2(decoder_1_out2), .out3(decoder_1_out3),
    .out4(decoder_1_out4), .out5(decoder_1_out5), .out6(decoder_1_out6), .out7(decoder_1_out7),
    .sel(DESTINATION));  // open: en
  Register u_AX (.D(multiplexer_1_out), .en(decoder_1_out0), .Q(AX), .clk(CLK));  // open: clr
  Register BX (.D(multiplexer_1_out), .en(decoder_1_out1), .Q(BX_q), .clk(CLK));  // open: clr
  Register CX (.D(multiplexer_1_out), .en(decoder_1_out2), .Q(CX_q), .clk(CLK));  // open: clr
  Register DX (.D(multiplexer_1_out), .en(decoder_1_out3), .Q(DX_q), .clk(CLK));  // open: clr
  Register PC (.D(multiplexer_1_out), .en(decoder_1_out4), .Q(PC_q), .clk(CLK));  // open: clr
  Register P1 (.D(multiplexer_1_out), .en(decoder_1_out5), .Q(P1_q), .clk(CLK));  // open: clr
  Register P2 (.D(multiplexer_1_out), .en(decoder_1_out6), .Q(P2_q), .clk(CLK));  // open: clr
  Register P3 (.D(multiplexer_1_out), .en(decoder_1_out7), .Q(P3_q), .clk(CLK));  // open: clr
  Multiplexer #(.select(3), .width(8)) multiplexer_2 (
    .in0(AX), .in1(BX_q), .in2(CX_q), .in3(DX_q), .in4(PC_q), .in5(P1_q), .in6(P2_q), .in7(P3_q),
    .out(VALUE1), .sel(SOURCE1));  // open: en
  Multiplexer #(.select(3), .width(8)) multiplexer_3 (
    .in0(AX), .in1(BX_q), .in2(CX_q), .in3(DX_q), .in4(PC_q), .in5(P1_q), .in6(P2_q), .in7(P3_q),
    .out(VALUE2), .sel(SOURCE2));  // open: en
endmodule
