// Logisim project Flags.circ as structural Verilog: 1 circuit, main circuit Flags
// FLAGS
module Flags (
  input  CLK,
  input  [3:0] ZCOP,
  output PF__Parity_Flag,
  output OF__Overflow_Flag,
  output CF__Carry_Flag,
  output ZF__Zero_Flag
);

  D_Flip_Flop ZF (.clk(CLK), .D(ZCOP[3]), .Q(ZF__Zero_Flag));  // open: Qn, preset, en, reset
  D_Flip_Flop CF (.clk(CLK), .D(ZCOP[2]), .Q(CF__Carry_Flag));  // open: Qn, preset, en, reset
  D_Flip_Flop OF (.clk(CLK), .D(ZCOP[1]), .Q(OF__Overflow_Flag));  // open: Qn, preset, en, reset
  D_Flip_Flop PF (.clk(CLK), .D(ZCOP[0]), .Q(PF__Parity_Flag));  // open: Qn, preset, en, reset
endmodule
