// Logisim project Memory.circ as structural Verilog: 1 circuit, main circuit Memory
module Memory (
  input  [7:0] Adress,
  input  [7:0] in_2,
  input  LD,
  output [7:0] out_4
);

  wire clock_1_out;

  Clock clock_1 (.out(clock_1_out));
  RAM #(.bus("separate")) ram_1 (
    .addr(Adress), .din(in_2), .data(out_4), .clk(clock_1_out), .ld(LD));  // open: str, sel, clr
endmodule
