// Logisim project Registers.circ as structural Verilog: 1 circuit, main circuit Registers
// REG
module Registers (
  input  CLK,
  input  [7:0] ALU,
  input  [7:0] DATA,
  input  L__if_1__input_from_DATA_to_REG_is_allowed,
  input  IF__if_1__input_into_REG_is_forbidden,
  input  MV__if_1__transfer_data_within_REG_is_allowed,
  input  [2:0] A1__Adress_of_first_register,
  input  [2:0] A2__Adress_of_second_register,
  input  [2:0] DEST__Adress_if_register_that_loads_data,
  input  S__if_1__Input_from_REG_to_DATA_is_allowed,
  output [7:0] AX,
  output [7:0] R1__Value_of_first_register,
  output [7:0] R2__Value_of_second_register
);

  wire and_1_out, decoder_1_out0, decoder_1_out1, decoder_1_out2, decoder_1_out3, decoder_1_out4,
       decoder_1_out5, decoder_1_out6, decoder_1_out7, not_1_out, not_2_out;
  wire [7:0] BX_q, controlled_buffer_1_out, controlled_buffer_2_out, CX_q, DX_q, multiplexer_1_out,
       multiplexer_2_out, P1_q, P2_q, P3_q, PC_q;

  Multiplexer #(.width(8)) multiplexer_1 (
    .in0(ALU), .in1(DATA), .out(multiplexer_1_out), .sel(L__if_1__input_from_DATA_to_REG_is_allowed));  // open: en
  assign controlled_buffer_1_out = MV__if_1__transfer_data_within_REG_is_allowed ? R1__Value_of_first_register : 8'bz;  // Controlled_Buffer controlled_buffer_1
  not not_1 (not_1_out, MV__if_1__transfer_data_within_REG_is_allowed);
  Multiplexer #(.width(8)) multiplexer_2 (
    .in0(controlled_buffer_1_out), .in1(multiplexer_1_out), .out(multiplexer_2_out), .sel(and_1_out));  // open: en
  and and_1 (and_1_out, not_1_out, S__if_1__Input_from_REG_to_DATA_is_allowed);
  not not_2 (not_2_out, IF__if_1__input_into_REG_is_forbidden);
  Decoder #(.select(3)) decoder_1 (
    .out0(decoder_1_out0), .out1(decoder_1_out1), .out2(decoder_1_out2), .out3(decoder_1_out3),
    .out4(decoder_1_out4), .out5(decoder_1_out5), .out6(decoder_1_out6), .out7(decoder_1_out7),
    .sel(DEST__Adress_if_register_that_loads_data));  // open: en
  assign controlled_buffer_2_out = not_2_out ? multiplexer_2_out : 8'bz;  // Controlled_Buffer controlled_buffer_2
  Register u_AX (.D(controlled_buffer_2_out), .en(decoder_1_out0), .Q(AX), .clk(CLK));  // open: clr
  Register BX (.D(controlled_buffer_2_out), .en(decoder_1_out1), .Q(BX_q), .clk(CLK));  // open: clr
  Register CX (.D(controlled_buffer_2_out), .en(decoder_1_out2), .Q(CX_q), .clk(CLK));  // open: clr
  Register DX (.D(controlled_buffer_2_out), .en(decoder_1_out3), .Q(DX_q), .clk(CLK));  // open: clr
  Register PC (.D(controlled_buffer_2_out), .en(decoder_1_out4), .Q(PC_q), .clk(CLK));  // open: clr
  Register P1 (.D(controlled_buffer_2_out), .en(decoder_1_out5), .Q(P1_q), .clk(CLK));  // open: clr
  Register P2 (.D(controlled_buffer_2_out), .en(decoder_1_out6), .Q(P2_q), .clk(CLK));  // open: clr
  Register P3 (.D(controlled_buffer_2_out), .en(decoder_1_out7), .Q(P3_q), .clk(CLK));  // open: clr
  Multiplexer #(.select(3), .width(8)) multiplexer_3 (
    .in0(AX), .in1(BX_q), .in2(CX_q), .in3(DX_q), .in4(PC_q), .in5(P1_q), .in6(P2_q), .in7(P3_q),
    .out(R1__Value_of_first_register), .sel(A1__Adress_of_first_register));  // open: en
  Multiplexer #(.select(3), .width(8)) multiplexer_4 (
    .in0(AX), .in1(BX_q), .in2(CX_q), .in3(DX_q), .in4(PC_q), .in5(P1_q), .in6(P2_q), .in7(P3_q),
    .out(R2__Value_of_second_register), .sel(A2__Adress_of_second_register));  // open: en
endmodule
