// Logisim project PC.circ as structural Verilog: 1 circuit, main circuit main
// PC
module main (
  input  CLK,
  input  [7:0] JMP__Input_for_JMP_command,
  input  J__if_1__JMP_is_allowed,
  input  CJ__if_1__JMP_is_allowed,
  output [7:0] CL__current_line
);

  wire and_1_out, and_2_out, and_3_out, and_4_out, and_5_out, and_6_out, and_7_out, not_1_out, not_2_out,
       not_3_out, not_4_out, not_5_out, not_6_out, not_7_out, not_8_out, not_9_out;
  wire [7:0] controlled_buffer_1_out;

  assign controlled_buffer_1_out = and_2_out ? JMP__Input_for_JMP_command : 8'bz;  // Controlled_Buffer controlled_buffer_1
  T_Flip_Flop t_ff_1 (
    .clk(CLK), .T(CLK), .Q(CL__current_line[0]), .preset(controlled_buffer_1_out[0]), .reset(not_1_out));  // open: Qn, en
  not not_1 (not_1_out, controlled_buffer_1_out[0]);
  T_Flip_Flop t_ff_2 (
    .clk(CLK), .T(CL__current_line[0]), .Q(CL__current_line[1]), .preset(controlled_buffer_1_out[1]),
    .reset(not_2_out));  // open: Qn, en
  not not_2 (not_2_out, controlled_buffer_1_out[1]);
  not not_3 (not_3_out, CLK);
  and and_1 (and_1_out, CL__current_line[1], CL__current_line[0]);
  not not_4 (not_4_out, controlled_buffer_1_out[2]);
  and and_2 (and_2_out, CJ__if_1__JMP_is_allowed, not_3_out, J__if_1__JMP_is_allowed);
  T_Flip_Flop t_ff_3 (
    .clk(CLK), .T(and_1_out), .Q(CL__current_line[2]), .preset(controlled_buffer_1_out[2]), .reset(not_4_out));  // open: Qn, en
  and and_3 (and_3_out, CL__current_line[2], and_1_out);
  T_Flip_Flop t_ff_4 (
    .clk(CLK), .T(and_3_out), .Q(CL__current_line[3]), .preset(controlled_buffer_1_out[3]), .reset(not_5_out));  // open: Qn, en
  not not_5 (not_5_out, controlled_buffer_1_out[3]);
  T_Flip_Flop t_ff_5 (
    .clk(CLK), .T(and_4_out), .Q(CL__current_line[4]), .preset(controlled_buffer_1_out[4]), .reset(not_6_out));  // open: Qn, en
  and and_4 (and_4_out, CL__current_line[3], and_3_out);
  not not_6 (not_6_out, controlled_buffer_1_out[4]);
  and and_5 (and_5_out, CL__current_line[4], and_4_out);
  T_Flip_Flop t_ff_6 (
    .clk(CLK), .T(and_5_out), .Q(CL__current_line[5]), .preset(controlled_buffer_1_out[5]), .reset(not_7_out));  // open: Qn, en
  and and_6 (and_6_out, CL__current_line[5], and_5_out);
  not not_7 (not_7_out, controlled_buffer_1_out[5]);
  T_Flip_Flop t_ff_7 (
    .clk(CLK), .T(and_6_out), .Q(CL__current_line[6]), .preset(controlled_buffer_1_out[6]), .reset(not_8_out));  // open: Qn, en
  not not_8 (not_8_out, controlled_buffer_1_out[6]);
  T_Flip_Flop t_ff_8 (
    .clk(CLK), .T(and_7_out), .Q(CL__current_line[7]), .preset(controlled_buffer_1_out[7]), .reset(not_9_out));  // open: Qn, en
  and and_7 (and_7_out, CL__current_line[6], and_6_out);
  not not_9 (not_9_out, controlled_buffer_1_out[7]);
endmodule
