// Logisim project SUB.circ as structural Verilog
// HS
module Half_Subtractor (
  input  X,
  input  Y,
  output S,
  output P
);

  wire not_1_out;

  xor xor_1 (S, X, Y);
  not not_1 (not_1_out, X);
  and and_1 (P, not_1_out, Y);
endmodule

// FS
module Full_Subtractor (
  input  P,
  input  X,
  input  Y,
  output S,
  output PP
);

  wire half_subtractor_1_p, half_subtractor_1_s, half_subtractor_2_p;

  Half_Subtractor half_subtractor_1 (.X(X), .Y(Y), .S(half_subtractor_1_s), .P(half_subtractor_1_p));
  Half_Subtractor half_subtractor_2 (.X(P), .Y(half_subtractor_1_s), .S(S), .P(half_subtractor_2_p));
  or or_1 (PP, half_subtractor_2_p, half_subtractor_1_p);
endmodule
