// Logisim project procesor.circ as structural Verilog
module Procesor (
  output [3:0] out_1,
  output [7:0] out_2,
  output [7:0] out_3
);

  wire alu_1_p6, CLK_out, main_2_l__if_1__input_from_data_to_reg_is_allowed,
       main_2_mv__if_1__transfer_data_within_reg_is_allowed,
       main_2_s__if_1__input_from_reg_to_data_is_allowed, not_1_out, not_2_out, not_3_out, registers_1_p9,
       registers_1_p10, undriven;
  wire [2:0] main_2_a1__adress_of_first_register, main_2_a2__adress_of_second_register,
       main_2_dest__adress_of_register_that_loads_data;
  wire [3:0] alu_1_p5, main_2_com__value_of_command__0000_to_1111;
  wire [7:0] main_1_cl__current_line, main_2_ma__adress_in_data_for_load, multiplexer_1_out, ram_2_data;
  wire [15:0] ram_1_data;

  Clock CLK (.out(CLK_out));
  PC_main main_1 (
    .CLK(CLK_out), .CL__current_line(main_1_cl__current_line), .JMP__Input_for_JMP_command(out_2),
    .CJ__if_1__JMP_is_allowed(undriven));
  not not_1 (not_1_out, 1'b1);
  CU_main main_2 (
    .INS__Instruction_value(ram_1_data),
    .COM__Value_of_command__0000_to_1111(main_2_com__value_of_command__0000_to_1111),
    .A1__Adress_of_first_register(main_2_a1__adress_of_first_register),
    .A2__Adress_of_second_register(main_2_a2__adress_of_second_register),
    .MA__Adress_in_DATA_for_LOAD(main_2_ma__adress_in_data_for_load),
    .DEST__Adress_of_register_that_loads_data(main_2_dest__adress_of_register_that_loads_data),
    .S__if_1__input_from_REG_to_DATA_is_allowed(main_2_s__if_1__input_from_reg_to_data_is_allowed),
    .MV__if_1__transfer_data_within_REG_is_allowed(main_2_mv__if_1__transfer_data_within_reg_is_allowed),
    .L__if_1__input_from_DATA_to_REG_is_allowed(main_2_l__if_1__input_from_data_to_reg_is_allowed));
  RAM #(.dataWidth(16), .bus("separate")) ram_1 (
    .addr(main_1_cl__current_line), .data(ram_1_data), .str(not_1_out), .clk(CLK_out), .ld(1'b1));  // open: din, sel, clr
  not not_2 (not_2_out, main_2_s__if_1__input_from_reg_to_data_is_allowed);
  Multiplexer #(.width(8)) multiplexer_1 (
    .in0(out_2), .in1(ram_2_data), .out(multiplexer_1_out),
    .sel(main_2_l__if_1__input_from_data_to_reg_is_allowed));  // open: en
  RAM #(.bus("separate")) ram_2 (
    .addr(main_2_ma__adress_in_data_for_load), .din(out_3), .data(ram_2_data),
    .str(main_2_s__if_1__input_from_reg_to_data_is_allowed), .clk(CLK_out), .ld(not_2_out));  // open: sel, clr
  not not_3 (not_3_out, main_2_s__if_1__input_from_reg_to_data_is_allowed);
  // Registers registers_1: pin names not known; wires that end beside it: multiplexer_1_out, main_2_a1__adress_of_first_register, main_2_a2__adress_of_second_register, main_2_dest__adress_of_register_that_loads_data, CLK_out, main_2_mv__if_1__transfer_data_within_reg_is_allowed, not_3_out, out_3, registers_1_p9, registers_1_p10
  // ALU alu_1: pin names not known; wires that end beside it: registers_1_p9, registers_1_p10, main_2_com__value_of_command__0000_to_1111, out_2, alu_1_p5, alu_1_p6
  Flags flags_1 (.ZCOP_out(out_1), .ZCOP(alu_1_p5), .CLK(CLK_out));
endmodule
